// Logisim project Main.circ as structural Verilog
module registerBank (
  input  AR_SPSel,
  input  ALUtoPC,
  input  ALUtoSP,
  input  ALUsub,
  input  ALUtoRR,
  input  RRClr,
  input  [1:0] ALUINSel,
  input  ALUtoAC,
  input  RBClk,
  input  [2:0] regLdS,
  input  [2:0] DBSel,
  output SPZ,
  output ACZ,
  output [9:0] IRtoCU
);

  wire decoder_1_out0, decoder_1_out1, decoder_1_out2, decoder_1_out3, decoder_1_out4, decoder_1_out5,
       decoder_1_out6, decoder_1_out7;
  wire [6:0] AR_q, PC_q, SP_q;
  wire [9:0] AC_q, alu_1_input, bit_extender_1_out, bit_extender_2_out, multiplexer_2_out, multiplexer_3_out,
       multiplexer_4_out, multiplexer_5_out, multiplexer_16_out, ram_1_data, RR_q, undriven;

  ALU alu_1 (.Input(alu_1_input), .Sub(ALUsub), .Output(undriven));
  Multiplexer #(.select(2), .width(10), .enable("false")) multiplexer_1 (
    .in0(AC_q), .in1(RR_q), .in2(bit_extender_1_out), .in3(bit_extender_2_out), .out(alu_1_input),
    .sel(ALUINSel));
  Decoder #(.select(3), .enable("false")) decoder_1 (
    .out0(decoder_1_out0), .out1(decoder_1_out1), .out2(decoder_1_out2), .out3(decoder_1_out3),
    .out4(decoder_1_out4), .out5(decoder_1_out5), .out6(decoder_1_out6), .out7(decoder_1_out7), .sel(regLdS));
  Multiplexer #(.width(10), .enable("false")) multiplexer_2 (
    .in0(multiplexer_16_out), .in1(undriven), .out(multiplexer_2_out), .sel(ALUtoPC));
  Multiplexer #(.width(10), .enable("false")) multiplexer_3 (
    .in0(multiplexer_16_out), .in1(undriven), .out(multiplexer_3_out), .sel(ALUtoSP));
  Multiplexer #(.width(10), .enable("false")) multiplexer_4 (
    .in0(multiplexer_16_out), .in1(undriven), .out(multiplexer_4_out), .sel(ALUtoRR));
  Multiplexer #(.width(10), .enable("false")) multiplexer_5 (
    .in0(multiplexer_16_out), .in1(undriven), .out(multiplexer_5_out), .sel(ALUtoAC));
  assign bit_extender_1_out = {{3{1'b0}}, SP_q};  // Bit_Extender bit_extender_1
  Register #(.width(7)) AR (.D(multiplexer_16_out[6:0]), .en(decoder_1_out0), .Q(AR_q), .clk(RBClk));  // open: clr
  assign bit_extender_2_out = {{3{1'b0}}, PC_q};  // Bit_Extender bit_extender_2
  Register #(.width(7)) PC (.D(multiplexer_2_out[6:0]), .en(decoder_1_out1), .Q(PC_q), .clk(RBClk));  // open: clr
  Register #(.width(7)) SP (.D(multiplexer_3_out[6:0]), .en(decoder_1_out2), .Q(SP_q), .clk(RBClk));  // open: clr
  Register #(.width(10)) RR (.D(multiplexer_4_out), .en(decoder_1_out3), .Q(RR_q), .clk(RBClk), .clr(RRClr));
  Register #(.width(10)) AC (.D(multiplexer_5_out), .en(decoder_1_out4), .Q(AC_q), .clk(RBClk));  // open: clr
  Register #(.width(10)) IR (.D(multiplexer_16_out), .en(decoder_1_out5), .Q(IRtoCU), .clk(RBClk));  // open: clr
  RAM #(.addrWidth(7), .dataWidth(10), .bus("separate")) ram_1 (
    .addr(SP_q), .din(multiplexer_16_out), .data(ram_1_data), .str(decoder_1_out6), .sel(1'b1), .clk(RBClk),
    .ld(decoder_1_out7), .clr(1'b0));
  Multiplexer #(.width(7), .enable("false")) multiplexer_6 (.in0(AR_q), .in1(SP_q), .out(SP_q), .sel(AR_SPSel));
  Multiplexer #(.select(3), .enable("false")) multiplexer_7 (
    .in0(1'b0), .in1(ram_1_data[9]), .in2(IRtoCU[9]), .in3(AC_q[9]), .in4(RR_q[9]), .in5(1'b0), .in6(1'b0),
    .in7(1'b0), .out(multiplexer_16_out[9]), .sel(DBSel));
  Multiplexer #(.select(3), .enable("false")) multiplexer_8 (
    .in0(1'b0), .in1(ram_1_data[8]), .in2(IRtoCU[8]), .in3(AC_q[8]), .in4(RR_q[8]), .in5(1'b0), .in6(1'b0),
    .in7(1'b0), .out(multiplexer_16_out[8]), .sel(DBSel));
  Multiplexer #(.select(3), .enable("false")) multiplexer_9 (
    .in0(1'b0), .in1(ram_1_data[7]), .in2(IRtoCU[7]), .in3(AC_q[7]), .in4(RR_q[7]), .in5(1'b0), .in6(1'b0),
    .in7(1'b0), .out(multiplexer_16_out[7]), .sel(DBSel));
  Multiplexer #(.select(3), .enable("false")) multiplexer_10 (
    .in0(1'b0), .in1(ram_1_data[6]), .in2(IRtoCU[6]), .in3(AC_q[6]), .in4(RR_q[6]), .in5(SP_q[6]),
    .in6(PC_q[6]), .in7(AR_q[6]), .out(multiplexer_16_out[6]), .sel(DBSel));
  Multiplexer #(.select(3), .enable("false")) multiplexer_11 (
    .in0(1'b0), .in1(ram_1_data[5]), .in2(IRtoCU[5]), .in3(AC_q[5]), .in4(RR_q[5]), .in5(SP_q[5]),
    .in6(PC_q[5]), .in7(AR_q[5]), .out(multiplexer_16_out[5]), .sel(DBSel));
  Multiplexer #(.select(3), .enable("false")) multiplexer_12 (
    .in0(1'b0), .in1(ram_1_data[4]), .in2(IRtoCU[4]), .in3(AC_q[4]), .in4(RR_q[4]), .in5(SP_q[4]),
    .in6(PC_q[4]), .in7(AR_q[4]), .out(multiplexer_16_out[4]), .sel(DBSel));
  Multiplexer #(.select(3), .enable("false")) multiplexer_13 (
    .in0(1'b0), .in1(ram_1_data[3]), .in2(IRtoCU[3]), .in3(AC_q[3]), .in4(RR_q[3]), .in5(SP_q[3]),
    .in6(PC_q[3]), .in7(AR_q[3]), .out(multiplexer_16_out[3]), .sel(DBSel));
  Multiplexer #(.select(3), .enable("false")) multiplexer_14 (
    .in0(1'b0), .in1(ram_1_data[2]), .in2(IRtoCU[2]), .in3(AC_q[2]), .in4(RR_q[2]), .in5(SP_q[2]),
    .in6(PC_q[2]), .in7(AR_q[2]), .out(multiplexer_16_out[2]), .sel(DBSel));
  Multiplexer #(.select(3), .enable("false")) multiplexer_15 (
    .in0(1'b0), .in1(ram_1_data[1]), .in2(IRtoCU[1]), .in3(AC_q[1]), .in4(RR_q[1]), .in5(SP_q[1]),
    .in6(PC_q[1]), .in7(AR_q[1]), .out(multiplexer_16_out[1]), .sel(DBSel));
  Multiplexer #(.select(3), .enable("false")) multiplexer_16 (
    .in0(1'b0), .in1(ram_1_data[0]), .in2(IRtoCU[0]), .in3(AC_q[0]), .in4(RR_q[0]), .in5(SP_q[0]),
    .in6(PC_q[0]), .in7(AR_q[0]), .out(multiplexer_16_out[0]), .sel(DBSel));
  nand nand_1 (SPZ, SP_q[0], SP_q[1], SP_q[2], SP_q[3], SP_q[4], SP_q[5], SP_q[6]);
  nand nand_2 (ACZ, AC_q[0], AC_q[1], AC_q[2], AC_q[3], AC_q[4], AC_q[5], AC_q[6], AC_q[7], AC_q[8], AC_q[9]);

  // Notes on the sheet:
  //   DB sel = 7
  //   DB sel = 6
  //   DB sel = 5
  //   DB sel = 4
  //   DB sel = 3
  //   DB sel = 2
  //   DB sel = 1
endmodule

module ALU (
  input  [9:0] Output,
  input  Sub,
  output [9:0] Input
);

  wire [9:0] multiplexer_1_out;

  Multiplexer #(.width(10), .enable("false")) multiplexer_1 (
    .in0(10'h1), .in1({10{1'b1}}), .out(multiplexer_1_out), .sel(Sub));
  Adder #(.width(10)) adder_1 (.a(Input), .b(multiplexer_1_out), .out(Output));  // open: cin, cout
endmodule
